# Fritzing sketch hd44780_lcd (saved by Fritzing 0.9.3b)
stripboards: 1

parts:
  ->_PIC = female pin header, 8 pins [form="♀ (female)"]
  5V_______G = double row male pin header, 6 pins [form="♂ (male)"]
  J3 = male pin header, 2 pins [form="♂ (male)"]
  LCD1 = LCD screen  # not connected
  U1 = 74HC595 [package="DIP16 [THT]"]
  J4 = female pin header, 16 pins [form="♀ (female)"]
  R1 = Resistor [tolerance=±5% resistance=220 package="2010 [SMD]"]
  R2 = Trimmer Potentiometer [maximum_resistance=10kΩ package=THT]

nets:
  N1: ->_PIC.pin1, J3.pin1
  N2: ->_PIC.pin2, J3.pin2
  N3: ->_PIC.pin4, 5V_______G.pin1, U1.MR, U1.VCC, J4.pin2, R1.Pin_1, R2.leg1
  N4: ->_PIC.pin5, 5V_______G.pin6, U1.GND, U1.OE, J4.pin1, J4.pin5, J4.pin16, R2.leg2
  N5: ->_PIC.pin6, U1.DS
  N6: ->_PIC.pin7, U1.SH_CP, U1.ST_CP
  N7: ->_PIC.pin8, J4.pin6
  N8: U1.Q2, J4.pin4
  N9: U1.Q3, J4.pin14
  N10: U1.Q4, J4.pin13
  N11: U1.Q5, J4.pin12
  N12: U1.Q6, J4.pin11
  N13: J4.pin3, R2.wiper
  N14: J4.pin15, R1.Pin_0
